# Fritzing sketch schema-di-montaggio (saved by Fritzing 0.9.10b)
breadboards: 1

parts:
  U1 = ESP32S-HiLetgo [part_number=ESP32S-HiLetgo]
  Part1 = KY-037 High Sensitivity Sound Detection Module [package="Breakout board"]
  OLED1 = OLED 128x64 I2C Monochrome Display

nets:
  N1: U1.GPIO11, Part1.G, OLED1.GND
  VIN: U1.VIN, Part1.+, OLED1.VDD
  N2: U1.GPIO15, Part1.A0
  N3: U1.GPIO21, OLED1.SDA
  N4: U1.GPIO22, OLED1.SCK

custom parts:
  ESP32S-HiLetgo: HiLetgo ESP-WROOM-32 ESP32 ESP-32S Development Board 2.4GHz Dual-Mode WiFi + Bluetooth Dual Cores Microcontroller The ESP32 integrated with Antenna switches, RF Balun, power amplifiers, low-noise amplifiers, filters, and management modules, and the entire solution occupies the least area of PCB. 2.4 GHz Wi-Fi plus Bluetooth dual-mode chip, with TSMC Ultra-low power consumption 40nm technology,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
  KY-037 High Sensitivity Sound Detection Module: KY-037 high sensitivity sound detection module is an analog/digital sensor that uses a condenser microphone to observe changes in environment noise.
